// Digital circuit main.dig as structural Verilog
module main (
  input  [7:0] Instruction_Binary,
  input  clk,
  input  Panic_Button,
  output [7:0] out_4
);

  wire undriven;
  wire [7:0] u_program_counter_data_out;

  program_counter #(.applicationType("IVERILOG"), .CodeFile("/home/kaldwin/Projects/the_electronics_project_misc/src/program_counter.v")) u_program_counter (
    .clk(clk), .data_in(u_program_counter_data_out), .reset(Panic_Button),
    .data_out(u_program_counter_data_out));
  memory_256x8 #(.applicationType("IVERILOG"), .CodeFile("/home/kaldwin/Development/Projects/the_electronics_project_misc/src/memory_256x8.v")) u_memory_256x8 (
    .clk(clk), .write(undriven), .address(u_program_counter_data_out), .data_in(Instruction_Binary),
    .data_out(out_4));

  // Notes on the sheet:
  //   clk: Hz: 5
endmodule
